// Logisim project ALU.circ as structural Verilog: 1 circuit, main circuit main
module main (
);

  wire comparator_1_eq, comparator_3_eq, decoder_1_out0, decoder_1_out1, decoder_1_out2, decoder_1_out3,
       decoder_1_out4, decoder_1_out5, decoder_1_out6, decoder_1_out7, decoder_2_out0, decoder_2_out1,
       decoder_2_out2, decoder_2_out3, decoder_2_out4, decoder_2_out5, decoder_2_out6, decoder_2_out7;
  wire [2:0] comparator_2_gt;
  wire [12:0] undriven_2;
  wire [15:0] adder_1_out, and_1_out, controlled_buffer_2_out, controlled_buffer_3_out, negator_1_out,
       or_1_out, subtractor_1_out, undriven, xor_1_out;

  Controlled_Buffer #(.width(16)) controlled_buffer_1 (.in(undriven));  // open: out, en
  Comparator #(.width(4)) comparator_1 (.a(4'b1111), .b(4'b1111), .eq(comparator_1_eq));  // open: gt, lt
  Decoder #(.select(3)) decoder_1 (
    .out0(decoder_1_out0), .out1(decoder_1_out1), .out2(decoder_1_out2), .out3(decoder_1_out3),
    .out4(decoder_1_out4), .out5(decoder_1_out5), .out6(decoder_1_out6), .out7(decoder_1_out7), .sel(3'b111),
    .en(comparator_1_eq));
  assign controlled_buffer_2_out = decoder_1_out0 ? {16{1'b1}} : 16'bz;  // Controlled_Buffer controlled_buffer_2
  Adder #(.width(16)) adder_1 (.a({16{1'b1}}), .b({16{1'b1}}), .out(adder_1_out));  // open: cin, cout
  Subtractor #(.width(16)) subtractor_1 (.a({16{1'b1}}), .b({16{1'b1}}), .out(subtractor_1_out));  // open: bin, bout
  assign xor_1_out = {16{1'b1}} ^ {16{1'b1}};  // XOR_Gate xor_1, 16 bits wide
  assign and_1_out = {16{1'b1}} & {16{1'b1}};  // AND_Gate and_1, 16 bits wide
  assign or_1_out = {16{1'b1}} | {16{1'b1}};  // OR_Gate or_1, 16 bits wide
  Negator #(.width(16)) negator_1 (.in({16{1'b1}}), .out(negator_1_out));
  Comparator #(.width(16)) comparator_2 (
    .a({16{1'b1}}), .b({16{1'b1}}), .gt(comparator_2_gt[0]), .eq(comparator_2_gt[1]), .lt(comparator_2_gt[2]));
  assign controlled_buffer_3_out = decoder_2_out0 ? {16{1'b1}} : 16'bz;  // Controlled_Buffer controlled_buffer_3
  Decoder #(.select(3)) decoder_2 (
    .out0(decoder_2_out0), .out1(decoder_2_out1), .out2(decoder_2_out2), .out3(decoder_2_out3),
    .out4(decoder_2_out4), .out5(decoder_2_out5), .out6(decoder_2_out6), .out7(decoder_2_out7), .sel(3'b111),
    .en(comparator_3_eq));
  Comparator #(.width(4)) comparator_3 (.a(4'b1111), .b(4'b1111), .eq(comparator_3_eq));  // open: gt, lt
  assign controlled_buffer_2_out = decoder_1_out1 ? adder_1_out : 16'bz;  // Controlled_Buffer controlled_buffer_4
  assign controlled_buffer_2_out = decoder_1_out2 ? subtractor_1_out : 16'bz;  // Controlled_Buffer controlled_buffer_5
  assign controlled_buffer_2_out = decoder_1_out3 ? xor_1_out : 16'bz;  // Controlled_Buffer controlled_buffer_6
  assign controlled_buffer_2_out = decoder_1_out4 ? and_1_out : 16'bz;  // Controlled_Buffer controlled_buffer_7
  assign controlled_buffer_2_out = decoder_1_out5 ? or_1_out : 16'bz;  // Controlled_Buffer controlled_buffer_8
  assign controlled_buffer_2_out = decoder_1_out6 ? negator_1_out : 16'bz;  // Controlled_Buffer controlled_buffer_9
  assign controlled_buffer_2_out = decoder_1_out7 ? {undriven_2, comparator_2_gt} : 16'bz;  // Controlled_Buffer controlled_buffer_10
  assign controlled_buffer_3_out = decoder_2_out7 ? {undriven_2, comparator_2_gt} : 16'bz;  // Controlled_Buffer controlled_buffer_11
  assign controlled_buffer_3_out = decoder_2_out6 ? negator_1_out : 16'bz;  // Controlled_Buffer controlled_buffer_12
  assign controlled_buffer_3_out = decoder_2_out5 ? or_1_out : 16'bz;  // Controlled_Buffer controlled_buffer_13
  assign controlled_buffer_3_out = decoder_2_out4 ? and_1_out : 16'bz;  // Controlled_Buffer controlled_buffer_14
  assign controlled_buffer_3_out = decoder_2_out3 ? xor_1_out : 16'bz;  // Controlled_Buffer controlled_buffer_15
  assign controlled_buffer_3_out = decoder_2_out2 ? subtractor_1_out : 16'bz;  // Controlled_Buffer controlled_buffer_16
  assign controlled_buffer_3_out = decoder_2_out1 ? adder_1_out : 16'bz;  // Controlled_Buffer controlled_buffer_17
endmodule
