// Logisim project Activation_Module.circ as structural Verilog: 2 circuits, main circuit main
module main (
  input  in_1,
  input  [7:0] in_2
);

  wire activationmodule_1_signal_out_1, activationmodule_1_signal_out_2, and_1_out, and_2_out, clock_1_out,
       not_1_out, not_2_out, not_3_out;
  wire [7:0] counter_1_q, dipswitch_1_sw8, register_1_q, register_2_q;

  Clock clock_1 (.out(clock_1_out));
  not not_1 (not_1_out, clock_1_out);
  DipSwitch dipswitch_1 (
    .sw1(dipswitch_1_sw8[7]), .sw2(dipswitch_1_sw8[6]), .sw3(dipswitch_1_sw8[5]), .sw4(dipswitch_1_sw8[4]),
    .sw5(dipswitch_1_sw8[3]), .sw6(dipswitch_1_sw8[2]), .sw7(dipswitch_1_sw8[1]), .sw8(dipswitch_1_sw8[0]));
  and and_1 (and_1_out, clock_1_out, not_2_out);
  not not_2 (not_2_out, clock_1_out);
  and and_2 (and_2_out, not_1_out, not_3_out);
  not not_3 (not_3_out, not_1_out);
  ActivationModule activationmodule_1 (
    .Signal_Out_2(activationmodule_1_signal_out_2), .Signal_Out_1(activationmodule_1_signal_out_1),
    .CLK_F(and_2_out), .Mode(in_1), .ctrl_line(dipswitch_1_sw8), .ctrl_seq(in_2), .CLK_R(and_1_out));
  Register #(.trigger("high")) register_1 (
    .D(counter_1_q), .clk(activationmodule_1_signal_out_1), .Q(register_1_q));  // open: en, clr
  Counter counter_1 (.Q(counter_1_q), .clk(clock_1_out));  // open: load, D, count, carry, up, clr
  Register #(.trigger("high")) register_2 (
    .D(register_1_q), .clk(activationmodule_1_signal_out_2), .Q(register_2_q));  // open: en, clr
  // Probe on register_2_q
endmodule

module ActivationModule (
  input  CLK_R,
  input  CLK_F,
  input  Mode,
  input  [7:0] ctrl_line,
  input  [7:0] ctrl_seq,
  output Signal_Out_1,
  output Signal_Out_2
);

  wire nor_1_out, not_1_out, or_1_out, or_2_out;
  wire [7:0] xor_1_out;

  not not_1 (not_1_out, Mode);
  assign xor_1_out = ctrl_line ^ ctrl_seq;  // XOR_Gate xor_1, 8 bits wide
  or or_1 (or_1_out, CLK_R, not_1_out);
  or or_2 (or_2_out, CLK_F, not_1_out);
  and and_1 (Signal_Out_1, or_1_out, nor_1_out);
  and and_2 (Signal_Out_2, or_2_out, nor_1_out);
  nor nor_1 (nor_1_out, xor_1_out[0], xor_1_out[1], xor_1_out[2], xor_1_out[3], xor_1_out[4], xor_1_out[5], xor_1_out[6], xor_1_out[7]);
endmodule
