// Logisim project logic_schematic.circ as structural Verilog: 5 circuits, main circuit main
module main (
  input  [15:0] in_1,
  input  [15:0] in_2,
  input  in_3,
  input  [15:0] in_4,
  input  [15:0] in_5,
  input  in_6,
  output [15:0] out_7
);

  wire bank_controller_1_oe, bank_controller_1_we, bank_module_x2_1_oe_out, bank_module_x2_1_we_out,
       bank_module_x2_2_oe_out, bank_module_x2_2_we_out, bank_module_x2_3_oe_out, bank_module_x2_3_we_out,
       bank_module_x4_1_oe_out, bank_module_x4_1_we_out;
  wire [7:0] bank_controller_1_id_out, bank_controller_1_pattern_out, bank_module_x2_1_id_out,
       bank_module_x2_1_pattern_out, bank_module_x2_2_id_out, bank_module_x2_2_pattern_out,
       bank_module_x2_3_id_out, bank_module_x2_3_pattern_out, bank_module_x4_1_id_out,
       bank_module_x4_1_pattern_out;
  wire [13:0] bank_controller_1_a_out, bank_module_x2_1_addr_out, bank_module_x2_3_addr_out,
       bank_module_x4_1_addr_out;
  wire [15:0] bank_controller_1_d_bank_out, bank_module_x2_1_d_out;

  Bank_Controller bank_controller_1 (
    .D_Mem_Out(out_7), .D_Bank_Out(bank_controller_1_d_bank_out), .A_Out(bank_controller_1_a_out),
    .OE(bank_controller_1_oe), .ID_Out(bank_controller_1_id_out),
    .Pattern_Out(bank_controller_1_pattern_out), .WE(bank_controller_1_we), .ID1_In(in_4), .ID2_In(in_5),
    .D_Mem_In(in_1), .A_In(in_2), .RW(in_3), .D_Bank_In(bank_module_x2_1_d_out), .Enable(in_6));
  Bank_Module_x2 bank_module_x2_1 (
    .ID_Out(bank_module_x2_1_id_out), .Pattern_Out(bank_module_x2_1_pattern_out),
    .OE_Out(bank_module_x2_1_oe_out), .WE_Out(bank_module_x2_1_we_out), .Addr_Out(bank_module_x2_1_addr_out),
    .D_Out(bank_module_x2_1_d_out), .Pattern_In(bank_controller_1_pattern_out),
    .ID_In(bank_controller_1_id_out), .OE_In(bank_controller_1_oe), .WE_In(bank_controller_1_we),
    .Addr_In(bank_controller_1_a_out), .D_In(bank_controller_1_d_bank_out));
  Bank_Module_x2 bank_module_x2_2 (
    .ID_Out(bank_module_x2_2_id_out), .Pattern_Out(bank_module_x2_2_pattern_out),
    .OE_Out(bank_module_x2_2_oe_out), .WE_Out(bank_module_x2_2_we_out), .D_Out(bank_module_x2_1_d_out),
    .Pattern_In(bank_module_x2_1_pattern_out), .ID_In(bank_module_x2_1_id_out),
    .OE_In(bank_module_x2_1_oe_out), .WE_In(bank_module_x2_1_we_out), .Addr_In(bank_module_x2_1_addr_out),
    .D_In(bank_controller_1_d_bank_out));  // open: Addr_Out
  Bank_Module_x4 bank_module_x4_1 (
    .ID_Out(bank_module_x4_1_id_out), .Pattern_Out(bank_module_x4_1_pattern_out),
    .OE_Out(bank_module_x4_1_oe_out), .WE_Out(bank_module_x4_1_we_out), .Addr_Out(bank_module_x4_1_addr_out),
    .D_Out(bank_module_x2_1_d_out), .Pattern_In(bank_module_x2_2_pattern_out),
    .ID_In(bank_module_x2_2_id_out), .OE_In(bank_module_x2_2_oe_out), .WE_In(bank_module_x2_2_we_out),
    .D_In(bank_controller_1_d_bank_out));  // open: Addr_In
  Bank_Module_x2 bank_module_x2_3 (
    .ID_Out(bank_module_x2_3_id_out), .Pattern_Out(bank_module_x2_3_pattern_out),
    .OE_Out(bank_module_x2_3_oe_out), .WE_Out(bank_module_x2_3_we_out), .Addr_Out(bank_module_x2_3_addr_out),
    .D_Out(bank_module_x2_1_d_out), .Pattern_In(bank_module_x4_1_pattern_out),
    .ID_In(bank_module_x4_1_id_out), .OE_In(bank_module_x4_1_oe_out), .WE_In(bank_module_x4_1_we_out),
    .Addr_In(bank_module_x4_1_addr_out), .D_In(bank_controller_1_d_bank_out));
endmodule

module Bank_Controller (
  input  [15:0] D_Mem_In,
  input  [15:0] D_Bank_In,
  input  [15:0] A_In,
  input  RW,
  input  Enable,
  input  [15:0] ID1_In,
  input  [15:0] ID2_In,
  output [7:0] Pattern_Out,
  output [15:0] D_Bank_Out,
  output [15:0] D_Mem_Out,
  output [13:0] A_Out,
  output OE,
  output WE,
  output [7:0] ID_Out
);

  wire and_2_out, not_1_out, not_2_out, not_3_out;

  not not_1 (not_1_out, RW);
  and and_1 (OE, A_In[15], not_1_out);
  and and_2 (and_2_out, A_In[15], RW);
  not not_2 (not_2_out, A_In[14]);
  assign ID_Out = not_2_out ? ID1_In[7:0] : 8'bz;  // Controlled_Buffer controlled_buffer_1
  not not_3 (not_3_out, not_2_out);
  assign ID_Out = not_3_out ? ID2_In[7:0] : 8'bz;  // Controlled_Buffer controlled_buffer_2
  and and_3 (WE, and_2_out, Enable);

  assign A_Out = A_In[13:0];
  assign D_Bank_Out = D_Mem_In;
  assign D_Mem_Out = D_Bank_In;
  assign Pattern_Out = {8{1'b0}};
endmodule

module Bank_Module_x4 (
  input  [13:0] Addr_In,
  input  [7:0] Pattern_In,
  input  [15:0] D_In,
  input  [7:0] ID_In,
  input  OE_In,
  input  WE_In,
  output [7:0] Pattern_Out,
  output [13:0] Addr_Out,
  output [15:0] D_Out,
  output [7:0] ID_Out,
  output OE_Out,
  output WE_Out
);

  wire nand_1_out, nand_2_out, nor_1_out, not_1_out, not_2_out;
  wire [7:0] xor_1_out;
  wire [15:0] ram_1_dout;

  Hex_Digit_Display hex_digit_display_1 (.value(Pattern_In[7:4]));  // open: dp
  Hex_Digit_Display hex_digit_display_2 (.value(Pattern_In[3:0]));  // open: dp
  Adder adder_1 (.a(8'h4), .b(Pattern_In), .out(Pattern_Out));  // open: cin, cout
  assign xor_1_out = Pattern_In ^ ID_In;  // XOR_Gate xor_1, 8 bits wide
  LED led_1 (.in(nor_1_out));
  nor nor_1 (nor_1_out, xor_1_out[2], xor_1_out[3], xor_1_out[4], xor_1_out[5], xor_1_out[6], xor_1_out[7]);
  nand nand_1 (nand_1_out, nor_1_out, WE_In);
  nand nand_2 (nand_2_out, nor_1_out, OE_In);
  not not_1 (not_1_out, nand_1_out);
  not not_2 (not_2_out, nand_2_out);
  RAM #(.addrWidth(16), .dataWidth(16), .trigger("high")) ram_1 (
    .addr({Pattern_In[1:0], Addr_In}), .we(not_1_out), .oe(not_2_out), .din(D_In), .dout(ram_1_dout));
  assign D_Out = not_2_out ? ram_1_dout : 16'bz;  // Controlled_Buffer controlled_buffer_1

  assign Addr_Out = Addr_In;
  assign ID_Out = ID_In;
  assign OE_Out = OE_In;
  assign WE_Out = WE_In;
endmodule

module Bank_Module_x2 (
  input  [13:0] Addr_In,
  input  [7:0] Pattern_In,
  input  [15:0] D_In,
  input  [7:0] ID_In,
  input  OE_In,
  input  WE_In,
  output [7:0] Pattern_Out,
  output [13:0] Addr_Out,
  output [15:0] D_Out,
  output [7:0] ID_Out,
  output OE_Out,
  output WE_Out
);

  wire nand_1_out, nand_2_out, nor_1_out, not_1_out, not_2_out;
  wire [7:0] xor_1_out;
  wire [15:0] ram_1_dout;

  Hex_Digit_Display hex_digit_display_1 (.value(Pattern_In[7:4]));  // open: dp
  Hex_Digit_Display hex_digit_display_2 (.value(Pattern_In[3:0]));  // open: dp
  Adder adder_1 (.a(8'h2), .b(Pattern_In), .out(Pattern_Out));  // open: cin, cout
  assign xor_1_out = Pattern_In ^ ID_In;  // XOR_Gate xor_1, 8 bits wide
  nor nor_1 (nor_1_out, xor_1_out[1], xor_1_out[2], xor_1_out[3], xor_1_out[4], xor_1_out[5], xor_1_out[6], xor_1_out[7]);
  LED led_1 (.in(nor_1_out));
  nand nand_1 (nand_1_out, nor_1_out, WE_In);
  nand nand_2 (nand_2_out, nor_1_out, OE_In);
  not not_1 (not_1_out, nand_1_out);
  not not_2 (not_2_out, nand_2_out);
  RAM #(.addrWidth(15), .dataWidth(16), .trigger("high")) ram_1 (
    .addr({Pattern_In[0], Addr_In}), .we(not_1_out), .oe(not_2_out), .din(D_In), .dout(ram_1_dout));
  assign D_Out = not_2_out ? ram_1_dout : 16'bz;  // Controlled_Buffer controlled_buffer_1

  assign Addr_Out = Addr_In;
  assign ID_Out = ID_In;
  assign OE_Out = OE_In;
  assign WE_Out = WE_In;
endmodule

module BID_Register (
  input  WE,
  input  Sup_In,
  input  S_BID,
  input  [15:0] BID_In,
  output [15:0] BID1_Out,
  output [15:0] BID2_Out
);

  wire and_1_out, and_2_out, and_3_out, not_1_out;

  and and_1 (and_1_out, WE, Sup_In);
  not not_1 (not_1_out, S_BID);
  Register #(.trigger("high"), .width(16)) register_1 (
    .D(BID_In), .en(and_2_out), .clk(and_2_out), .Q(BID1_Out));  // open: clr
  and and_2 (and_2_out, and_1_out, not_1_out);
  Register #(.trigger("high"), .width(16)) register_2 (
    .D(BID_In), .en(and_3_out), .clk(and_3_out), .Q(BID2_Out));  // open: clr
  and and_3 (and_3_out, and_1_out, S_BID);
endmodule
