// Logisim project register_file.circ as structural Verilog: 2 circuits, main circuit main
module main (
  input  in_1,
  input  [15:0] in_2,
  input  in_3,
  input  in_4,
  input  in_5,
  input  [2:0] in_6,
  input  in_7,
  input  [2:0] in_8,
  input  [2:0] in_9,
  input  [15:0] in_10,
  output out_11,
  output [15:0] out_12,
  output [15:0] out_13,
  output [15:0] out_14,
  output [15:0] out_15
);

  wire and_1_out, and_2_out, clock_1_out, not_1_out, not_2_out, not_3_out;

  not not_1 (not_1_out, clock_1_out);
  Clock clock_1 (.out(clock_1_out));
  RegisterFile registerfile_1 (
    .FLAG_Out(out_15), .B_Out(out_13), .A_Out(out_12), .Sup_Out(out_11), .IP_Out(out_14), .CLK_R(and_2_out),
    .CLK_F(and_1_out), .WE(in_1), .Const_In(in_10), .Const_Reg(in_4), .S_Sup(in_5), .R_Sup(in_7),
    .D_In(in_2), .D_Sel(in_6), .A_Sel(in_8), .B_Sel(in_9), .Zero_One(in_3));
  not not_2 (not_2_out, not_1_out);
  not not_3 (not_3_out, clock_1_out);
  and and_1 (and_1_out, not_1_out, not_2_out);
  and and_2 (and_2_out, clock_1_out, not_3_out);
endmodule

module RegisterFile (
  input  S_Sup,
  input  Zero_One,
  input  R_Sup,
  input  [15:0] D_In,
  input  CLK_R,
  input  CLK_F,
  input  WE,
  input  [15:0] Const_In,
  input  [2:0] D_Sel,
  input  Const_Reg,
  input  [2:0] A_Sel,
  input  [2:0] B_Sel,
  output Sup_Out,
  output [15:0] A_Out,
  output [15:0] B_Out,
  output [15:0] IP_Out,
  output [15:0] FLAG_Out
);

  wire and_1_out, and_2_out, and_3_out, and_4_out, and_5_out, and_6_out, and_7_out, and_8_out, and_9_out,
       and_10_out, decoder_1_out1, decoder_1_out2, decoder_1_out3, decoder_1_out4, decoder_1_out5,
       decoder_1_out6, decoder_1_out7, decoder_2_out0, decoder_2_out1, decoder_2_out2, decoder_2_out3,
       decoder_2_out4, decoder_2_out5, decoder_2_out6, decoder_2_out7, decoder_3_out0, decoder_3_out1,
       decoder_3_out2, decoder_3_out3, decoder_3_out4, decoder_3_out5, decoder_3_out6, decoder_3_out7,
       not_1_out;
  wire [7:0] register_1_q, register_1_q_2;
  wire [15:0] A_q, B_q, C_q, controlled_buffer_1_out, D_q, SP_q;

  Register #(.trigger("high"), .width(16)) register_1 (
    .D(D_In), .clk(and_1_out), .Q({register_1_q_2, register_1_q}));  // open: en, clr
  and and_1 (and_1_out, CLK_R, WE);
  and and_2 (and_2_out, CLK_F, WE);
  Decoder #(.select(3)) decoder_1 (
    .out1(decoder_1_out1), .out2(decoder_1_out2), .out3(decoder_1_out3), .out4(decoder_1_out4),
    .out5(decoder_1_out5), .out6(decoder_1_out6), .out7(decoder_1_out7), .sel(D_Sel));  // open: out0, en
  Decoder #(.select(3)) decoder_2 (
    .out0(decoder_2_out0), .out1(decoder_2_out1), .out2(decoder_2_out2), .out3(decoder_2_out3),
    .out4(decoder_2_out4), .out5(decoder_2_out5), .out6(decoder_2_out6), .out7(decoder_2_out7), .sel(A_Sel));  // open: en
  Decoder #(.select(3)) decoder_3 (
    .out0(decoder_3_out0), .out1(decoder_3_out1), .out2(decoder_3_out2), .out3(decoder_3_out3),
    .out4(decoder_3_out4), .out5(decoder_3_out5), .out6(decoder_3_out6), .out7(decoder_3_out7), .sel(B_Sel));  // open: en
  assign controlled_buffer_1_out = decoder_2_out0 ? {{15{1'b0}}, Zero_One} : 16'bz;  // Controlled_Buffer controlled_buffer_1
  assign B_Out = decoder_3_out0 ? {{15{1'b0}}, Zero_One} : 16'bz;  // Controlled_Buffer controlled_buffer_2
  Register #(.trigger("high"), .width(16)) IP (
    .D({register_1_q_2, register_1_q}), .clk(and_3_out), .Q(IP_Out));  // open: en, clr
  and and_3 (and_3_out, and_2_out, decoder_1_out1);
  Register #(.trigger("high"), .width(16)) SP (
    .D({register_1_q_2, register_1_q}), .clk(and_4_out), .Q(SP_q));  // open: en, clr
  and and_4 (and_4_out, and_2_out, decoder_1_out2);
  assign controlled_buffer_1_out = decoder_2_out1 ? IP_Out : 16'bz;  // Controlled_Buffer controlled_buffer_3
  assign B_Out = decoder_3_out1 ? IP_Out : 16'bz;  // Controlled_Buffer controlled_buffer_4
  assign controlled_buffer_1_out = decoder_2_out2 ? SP_q : 16'bz;  // Controlled_Buffer controlled_buffer_5
  assign B_Out = decoder_3_out2 ? SP_q : 16'bz;  // Controlled_Buffer controlled_buffer_6
  Register #(.trigger("high"), .width(16)) A (
    .D({register_1_q_2, register_1_q}), .clk(and_5_out), .Q(A_q));  // open: en, clr
  and and_5 (and_5_out, and_2_out, decoder_1_out3);
  assign controlled_buffer_1_out = decoder_2_out3 ? A_q : 16'bz;  // Controlled_Buffer controlled_buffer_7
  assign B_Out = decoder_3_out3 ? A_q : 16'bz;  // Controlled_Buffer controlled_buffer_8
  Register #(.trigger("high"), .width(16)) B (
    .D({register_1_q_2, register_1_q}), .clk(and_6_out), .Q(B_q));  // open: en, clr
  and and_6 (and_6_out, and_2_out, decoder_1_out4);
  Register #(.trigger("high"), .width(16)) C (
    .D({register_1_q_2, register_1_q}), .clk(and_7_out), .Q(C_q));  // open: en, clr
  and and_7 (and_7_out, and_2_out, decoder_1_out5);
  assign controlled_buffer_1_out = decoder_2_out4 ? B_q : 16'bz;  // Controlled_Buffer controlled_buffer_9
  assign B_Out = decoder_3_out4 ? B_q : 16'bz;  // Controlled_Buffer controlled_buffer_10
  assign controlled_buffer_1_out = decoder_2_out5 ? C_q : 16'bz;  // Controlled_Buffer controlled_buffer_11
  assign B_Out = decoder_3_out5 ? C_q : 16'bz;  // Controlled_Buffer controlled_buffer_12
  Register #(.trigger("high"), .width(16)) D (
    .D({register_1_q_2, register_1_q}), .clk(and_8_out), .Q(D_q));  // open: en, clr
  and and_8 (and_8_out, and_2_out, decoder_1_out6);
  and and_9 (and_9_out, and_2_out, decoder_1_out7);
  assign controlled_buffer_1_out = decoder_2_out6 ? D_q : 16'bz;  // Controlled_Buffer controlled_buffer_13
  assign B_Out = decoder_3_out6 ? D_q : 16'bz;  // Controlled_Buffer controlled_buffer_14
  Register #(.trigger("high")) FLAG_0 (.D(register_1_q_2), .clk(and_9_out), .Q(FLAG_Out[7:0]));  // open: en, clr
  and and_10 (and_10_out, and_9_out, FLAG_Out[15]);
  assign controlled_buffer_1_out = decoder_2_out7 ? FLAG_Out : 16'bz;  // Controlled_Buffer controlled_buffer_15
  assign B_Out = decoder_3_out7 ? FLAG_Out : 16'bz;  // Controlled_Buffer controlled_buffer_16
  D_Flip_Flop #(.trigger("high")) d_ff_1 (
    .D(register_1_q[7]), .clk(and_10_out), .Q(FLAG_Out[15]), .preset(S_Sup), .reset(R_Sup));  // open: Qn
  Register #(.trigger("high"), .width(7)) FLAG_1 (
    .D(register_1_q[6:0]), .clk(and_10_out), .Q(FLAG_Out[14:8]));  // open: en, clr
  not not_1 (not_1_out, Const_Reg);
  assign A_Out = not_1_out ? Const_In : 16'bz;  // Controlled_Buffer controlled_buffer_17
  assign A_Out = Const_Reg ? controlled_buffer_1_out : 16'bz;  // Controlled_Buffer controlled_buffer_18

  assign Sup_Out = FLAG_Out[15];
endmodule
